# Fritzing sketch nodearduino (saved by Fritzing 0.9.2b)
breadboards: 1

parts:
  R1 = Resistor [tolerance=±5% resistance=220 package=THT]
  Composant1 = Arduino Uno (Rev3)
  R2 = Photocell (LDR) [package=THT]

nets:
  N1: R1.Pin_0, Composant1.A0, R2.pin_1
  N2: R1.Pin_1, Composant1.GND
  N3: Composant1.5V, R2.pin_0
